// Logisim project GRP_6 2nd 30 MOD-60.circ as structural Verilog: 1 circuit, main circuit main
module main (
  input  LOGIC_0_1,
  input  ENABLE,
  output MSB,
  output E,
  output D,
  output C,
  output B,
  output LSB
);

  wire and_1_out, and_2_out, and_3_out, and_4_out, and_5_out, CLOCK_out;

  Clock CLOCK (.out(CLOCK_out));
  J_K_Flip_Flop A (
    .J(LOGIC_0_1), .clk(CLOCK_out), .K(LOGIC_0_1), .Q(LSB), .en(ENABLE), .reset(and_5_out));  // open: Qn, preset
  J_K_Flip_Flop u_B (.J(LSB), .clk(CLOCK_out), .K(LSB), .Q(B), .en(ENABLE), .reset(and_5_out));  // open: Qn, preset
  and and_1 (and_1_out, LSB, B);
  J_K_Flip_Flop u_C (
    .J(and_1_out), .clk(CLOCK_out), .K(and_1_out), .Q(C), .en(ENABLE), .reset(and_5_out));  // open: Qn, preset
  and and_2 (and_2_out, and_1_out, C);
  J_K_Flip_Flop u_D (
    .J(and_2_out), .clk(CLOCK_out), .K(and_2_out), .Q(D), .en(ENABLE), .reset(and_5_out));  // open: Qn, preset
  and and_3 (and_3_out, and_2_out, D);
  J_K_Flip_Flop u_E (
    .J(and_3_out), .clk(CLOCK_out), .K(and_3_out), .Q(E), .en(ENABLE), .reset(and_5_out));  // open: Qn, preset
  and and_4 (and_4_out, and_3_out, E);
  J_K_Flip_Flop F (
    .J(and_4_out), .clk(CLOCK_out), .K(and_4_out), .Q(MSB), .en(ENABLE), .reset(and_5_out));  // open: Qn, preset
  and and_5 (and_5_out, C, D, E, MSB);

  // Notes on the sheet:
  //   2ND 30 GROUP 6
  //   1903117
  //   1903118
  //   1903119
  //   1903120
  //   F
  //   MOD-60 Synchronus Up Counter JK-FF
  //   Up Counter
  //   A
endmodule
