// Logisim project GRP_6 2nd 30 NAND.circ as structural Verilog: 1 circuit, main circuit main
module main (
  input  A,
  input  B,
  output OUTPUT
);

  wire transistor_3_out;

  Transistor transistor_1 (.in(1'b1), .out(OUTPUT), .gate(B));
  Transistor #(.\type ("n")) transistor_2 (.in(transistor_3_out), .out(OUTPUT), .gate(A));
  Transistor #(.\type ("n")) transistor_3 (.in(1'b0), .out(transistor_3_out), .gate(B));
  Transistor #(.gate("br")) transistor_4 (.in(1'b1), .out(OUTPUT), .gate(A));

  // Notes on the sheet:
  //   2ND 30 GROUP 6
  //   1903117
  //   1903118
  //   1903119
  //   1903120
  //   2 INPUT CMOS NAND GATE
  //   +V
  //   DD
  //   P-MOS
  //   GROUND
  //   P-MOS
  //   ------------------------------------------------------------------------------------------------------------------------------------------------------------------------
  //   N-MOS
  //   N-MOS
  //   PULL UP NETWORK
  //   PULL DOWN NETWORK
endmodule
